# Fritzing sketch Rhythm_Division (saved by Fritzing 0.9.3b)
circuit board: 5cm x 10cm
breadboards: 1

parts:
  P1_50K_B = female pin header, 3 pins [form="♀ (female)"]
  R1 = Resistor [tolerance=±5% resistance=3.3k package=THT]
  R2 = Resistor [tolerance=±5% resistance=3.3k package=THT]
  R3 = Resistor [tolerance=±5% resistance=3.3k package=THT]
  R4 = Resistor [tolerance=±5% resistance=3.3k package=THT]
  P2_50K_B = female pin header, 3 pins [form="♀ (female)"]
  P3_50K_B = female pin header, 3 pins [form="♀ (female)"]
  P4_50K_B = female pin header, 3 pins [form="♀ (female)"]
  IC1 = IC, DIP package, 14 pins [chip_label=CD40106]
  IC2 = IC, DIP package, 14 pins [chip_label=4066]
  R5 = Resistor [tolerance=±5% resistance=22k package=THT]
  R6 = Resistor [tolerance=±5% resistance=22k package=THT]
  R7 = Resistor [tolerance=±5% resistance=22k package=THT]
  R8 = Resistor [tolerance=±5% resistance=22k package=THT]
  U1 = LM 358 Dual Op-Amp [package="DIP8 [THT]"]
  R9 = Resistor [tolerance=±5% resistance=1.5k package=THT]
  C5 = Electrolytic Capacitor [capacitance=1µF package="100 mil [THT, electrolytic]"]
  10K_A_(Vol) = female pin header, 3 pins [form="♀ (female)"]
  OUT = female pin header, 2 pins [form="♀ (female)"]
  R10 = Resistor [tolerance=±5% resistance=22k package=THT]
  R11 = Resistor [tolerance=±5% resistance=22k package=THT]
  C6 = Electrolytic Capacitor [capacitance=100µF package="100 mil [THT, electrolytic]"]
  IC3 = IC, DIP package, 16 pins [chip_label=4060]
  R12 = Resistor [tolerance=±5% resistance=3.3k package=THT]
  C7 = Electrolytic Capacitor [capacitance=1µF package="100 mil [THT, electrolytic]"]
  C8 = Electrolytic Capacitor [capacitance=1µF package="100 mil [THT, electrolytic]"]
  C9 = Electrolytic Capacitor [capacitance=1µF package="100 mil [THT, electrolytic]"]
  C10 = Electrolytic Capacitor [capacitance=1µF package="100 mil [THT, electrolytic]"]
  C11 = Electrolytic Capacitor [capacitance=1µF package="100 mil [THT, electrolytic]"]
  P5_50K_B1 = female pin header, 3 pins [form="♀ (female)"]
  R13 = Resistor [tolerance=±5% resistance=22k package=THT]
  R14 = Resistor [tolerance=±5% resistance=22k package=THT]
  R15 = Resistor [tolerance=±5% resistance=22k package=THT]
  R16 = Resistor [tolerance=±5% resistance=22k package=THT]
  IC4 = Voltage Regulator [package=to220-igo]
  Vin_12V-15V = female pin header, 2 pins [form="♀ (female)"]
  C12 = Electrolytic Capacitor [capacitance=100µF voltage=16V package="100 mil [THT, electrolytic]"]
  C13 = Electrolytic Capacitor [capacitance=100µF voltage=35V package="100 mil [THT, electrolytic]"]
  C3 = Ceramic Capacitor [capacitance=100nF package="200 mil [THT, multilayer]"]
  C2 = Ceramic Capacitor [capacitance=100nF package="200 mil [THT, multilayer]"]
  C4 = Ceramic Capacitor [capacitance=100nF package="200 mil [THT, multilayer]"]
  J1 = female pin header, 4 pins [form="♀ (female)"]
  J2 = female pin header, 4 pins [form="♀ (female)"]
  R17 = Resistor [tolerance=±5% resistance=10k package=THT]
  R18 = Resistor [tolerance=±5% resistance=18k package=THT]
  25K_B_(Tone) = female pin header, 3 pins [form="♀ (female)"]
  C14 = Ceramic Capacitor [capacitance=15nF package="200 mil [THT, multilayer]"]
  C15 = Ceramic Capacitor [capacitance=100nF package="200 mil [THT, multilayer]"]
  C1 = Ceramic Capacitor [capacitance=100nF package="200 mil [THT, multilayer]"]

nets:
  N1: P1_50K_B.pin1, P1_50K_B.pin2, R1.Pin_0
  N2: P1_50K_B.pin3, IC1.pin1, C1.1
  N3: R1.Pin_1, IC1.pin2, IC2.pin1
  N4: R2.Pin_0, P2_50K_B.pin1, P2_50K_B.pin2
  N5: R2.Pin_1, IC1.pin4, IC2.pin3
  N6: R3.Pin_0, P3_50K_B.pin1, P3_50K_B.pin2
  N7: R3.Pin_1, IC1.pin6, IC2.pin8
  N8: R4.Pin_0, IC1.pin8, IC2.pin10
  N9: R4.Pin_1, P4_50K_B.pin1, P4_50K_B.pin2
  N10: P2_50K_B.pin3, IC1.pin3, C2.1
  N11: P3_50K_B.pin3, IC1.pin5, C3.1
  N12: P4_50K_B.pin3, IC1.pin9, C4.1
  GND: IC1.pin7, IC2.pin7, U1.connector3, 10K_A_(Vol).pin3, OUT.pin2, R11.Pin_0, C6.-, IC3.pin8, IC3.pin12, C7.-, R13.Pin_0, R14.Pin_0, R15.Pin_0, R16.Pin_0, IC4.GND, Vin_12V-15V.pin1, C12.-, C13.-, C3.0, C2.0, C4.0, 25K_B_(Tone).pin3, C15.0, C1.0
  N13: IC1.pin10, IC3.pin11, R12.Pin_0
  N14: IC1.pin11, C7.+, P5_50K_B1.pin1, P5_50K_B1.pin2
  12V: IC1.pin14, IC2.pin14, U1.connector7, R10.Pin_1, IC3.pin16, IC4.OUT, C12.+, C15.1
  N15: IC2.pin2, R5.Pin_0
  N16: IC2.pin4, R6.Pin_0
  N17: IC2.pin5, R14.Pin_1, J1.pin3
  N18: IC2.pin6, R13.Pin_1, J1.pin4
  N19: IC2.pin9, R7.Pin_0
  N20: IC2.pin11, R8.Pin_0
  N21: IC2.pin12, R15.Pin_1, J1.pin2
  N22: IC2.pin13, R16.Pin_1, J1.pin1
  N23: R5.Pin_1, C8.-
  N24: R6.Pin_1, C9.-
  N25: R7.Pin_1, C10.-
  N26: R8.Pin_1, C11.-
  N27: U1.connector0, R9.Pin_1, R17.Pin_0
  N28: U1.connector1, R9.Pin_0, C8.+, C9.+, C10.+, C11.+
  N29: U1.connector2, R10.Pin_0, R11.Pin_1, C6.+
  N30: U1.connector4, R18.Pin_1, 25K_B_(Tone).pin1
  N31: U1.connector5, U1.connector6, C5.+
  N32: C5.-, 10K_A_(Vol).pin1
  N33: 10K_A_(Vol).pin2, OUT.pin1
  N34: IC3.pin4, J2.pin4
  N35: IC3.pin5, J2.pin3
  N36: IC3.pin6, J2.pin2
  N37: IC3.pin7, J2.pin1
  N38: R12.Pin_1, P5_50K_B1.pin3
  N39: IC4.IN, Vin_12V-15V.pin2, C13.+
  N40: R17.Pin_1, R18.Pin_0, C14.1
  N41: 25K_B_(Tone).pin2, C14.0

notes:
  To switches
